// Logisim project s-mips.circ as structural Verilog
module S_MIPS_Board (
  input  DESHABILITAR_DISPATCHER,
  output halt
);

  wire button_1_out, CLK, CS, d_ff_1_q, LCLR, LoadRAM, LoadRAMOn, LW, R_R_W, R_W, ram_dispatcher_1_finished,
       RCS, Reset_out, RST, TTY_EN;
  wire [2:0] KDB;
  wire [3:0] LMask, Mask, ram_1_read_time, ram_1_write_time, RMask;
  wire [6:0] KDB_DATA, TTY_DATA;
  wire [15:0] Addr, LAddr, RAddr;
  wire [31:0] I0, I1, I2, I3, LData, ram_1_data_out_0, ram_1_data_out_1, ram_1_data_out_2, ram_1_data_out_3,
       RI0, RI1, RI2, RI3;

  TTY #(.rows(25), .cols(80)) tty_1 (.data(TTY_DATA), .clk(CLK), .we(TTY_EN), .clr(RST));
  not not_1 (LoadRAMOn, ram_dispatcher_1_finished);
  RAM_Dispatcher ram_dispatcher_1 (
    .WriteTime(ram_1_write_time), .Clock(CLK), .Data(LData), .Address(LAddr), .Mask(LMask),
    .Finished(ram_dispatcher_1_finished), .Write(LW), .CLR(LCLR));
  Keyboard #(.buflen(64)) keyboard_1 (.clk(CLK), .re(KDB[0]), .avail(KDB[2]), .data(KDB_DATA));  // open: clr
  RAM ram_1 (
    .Address(RAddr), .Data_Out_0(ram_1_data_out_0), .Data_Out_1(ram_1_data_out_1),
    .Data_Out_2(ram_1_data_out_2), .Data_Out_3(ram_1_data_out_3), .Data_In_0(RI0), .Data_In_1(RI1),
    .Data_In_2(RI2), .Data_In_3(RI3), .Mask(RMask), .nRead_Write(R_R_W), .Chip_Select(RCS),
    .Read_Time(ram_1_read_time), .Reset(button_1_out), .Write_Time(ram_1_write_time));
  Button button_1 (.out(button_1_out));
  D_Flip_Flop d_ff_1 (.clk(CLK), .D(1'b1), .Q(d_ff_1_q), .reset(Reset_out));  // open: Qn, preset, en
  Button Reset (.out(Reset_out));
  S_MIPS s_mips_1 (
    .Kbd_Enable(KDB[0]), .Address(Addr), .Kbd_Clear(KDB[1]), .Kbd_Available(KDB[2]), .RAM_In_0(I0),
    .Kbd_ASCII_Data(KDB_DATA), .RAM_In_1(I1), .TTY_Enable(TTY_EN), .RAM_In_2(I2), .RAM_In_3(I3),
    .TTY_ASCII_Data(TTY_DATA), .Reset(RST), .RAM_Out_0(ram_1_data_out_0), .Clock(CLK),
    .RAM_Out_1(ram_1_data_out_1), .Stop(halt), .RAM_Out_2(ram_1_data_out_2), .RAM_Out_3(ram_1_data_out_3),
    .Mask(Mask), .Read_Time(ram_1_read_time), .Write_Time(ram_1_write_time), .nRead_Write(R_W),
    .Chip_Select(CS));
  D_Flip_Flop d_ff_2 (.clk(CLK), .D(d_ff_1_q), .Qn(LCLR), .reset(Reset_out));  // open: Q, preset, en
  or or_1 (RST, LCLR, LoadRAM);
  Clock clock_1 (.out(CLK));
  Multiplexer #(.width(32), .enable("false")) multiplexer_1 (.in0(I0), .in1(LData), .out(RI0), .sel(LoadRAM));
  Multiplexer #(.width(32), .enable("false")) multiplexer_2 (.in0(I1), .in1(LData), .out(RI1), .sel(LoadRAM));
  Multiplexer #(.width(32), .enable("false")) multiplexer_3 (.in0(I2), .in1(LData), .out(RI2), .sel(LoadRAM));
  Multiplexer #(.width(32), .enable("false")) multiplexer_4 (.in0(I3), .in1(LData), .out(RI3), .sel(LoadRAM));
  and and_1 (LoadRAM, ~DESHABILITAR_DISPATCHER, LoadRAMOn);  // AND_Gate
  Multiplexer #(.width(16), .enable("false")) multiplexer_5 (.in0(Addr), .in1(LAddr), .out(RAddr), .sel(LoadRAM));
  Multiplexer #(.width(4), .enable("false")) multiplexer_6 (.in0(Mask), .in1(LMask), .out(RMask), .sel(LoadRAM));
  Multiplexer #(.enable("false")) multiplexer_7 (.in0(CS), .in1(LW), .out(RCS), .sel(LoadRAM));
  Multiplexer #(.enable("false")) multiplexer_8 (.in0(R_W), .in1(LW), .out(R_R_W), .sel(LoadRAM));

  // Notes on the sheet:
  //   NO MODIFICAR
  //   Keyboard
endmodule

module RAM (
  input  [15:0] Address,
  input  [31:0] Data_In_0,
  input  [31:0] Data_In_1,
  input  [31:0] Data_In_2,
  input  [31:0] Data_In_3,
  input  [3:0] Mask,
  input  nRead_Write,
  input  Chip_Select,
  input  Reset,
  output [31:0] Data_Out_0,
  output [31:0] Data_Out_1,
  output [31:0] Data_Out_2,
  output [31:0] Data_Out_3,
  output [3:0] Read_Time,
  output [3:0] Write_Time
);

  wire and_2_out, and_3_out, and_4_out, and_5_out, and_6_out, and_7_out, and_8_out, and_9_out, Changed, CLK,
       comparator_2_eq, comparator_3_eq, comparator_4_eq, comparator_5_eq, comparator_6_eq, Count,
       demultiplexer_3_out0, Idle, Idle_q, Load, Load0, Load1, nand_1_out, or_1_out, or_2_out, or_3_out,
       or_4_out, or_5_out, or_6_out, or_7_out, or_8_out, or_9_out, or_10_out, Proc_q, Update_Mem, Zero_Time;
  wire [3:0] counter_1_q, multiplexer_1_out, subtractor_1_out;
  wire [31:0] register_1_q, register_2_q, register_3_q, register_4_q, register_5_q;

  // Probe on 4'b0011
  // Probe on 4'b0010
  Multiplexer #(.width(4), .enable("false")) multiplexer_1 (
    .in0(4'b0011), .in1(4'b0010), .out(multiplexer_1_out), .sel(nRead_Write));
  or or_1 (or_1_out, Idle, Update_Mem);
  or or_2 (or_2_out, ~Chip_Select, Reset);  // OR_Gate
  Subtractor #(.width(4)) subtractor_1 (.a(multiplexer_1_out), .b(4'b0010), .out(subtractor_1_out));  // open: bin, bout
  D_Flip_Flop u_Idle (.clk(CLK), .D(or_1_out), .Q(Idle_q), .preset(or_2_out));  // open: Qn, en, reset
  Demultiplexer #(.enable("false")) demultiplexer_1 (.out0(Idle), .out1(Load0), .in(Idle_q), .sel(Changed));
  // Probe on counter_1_q
  Counter #(.width(4), .max('hf)) counter_1 (
    .load(Load), .D(subtractor_1_out), .count(Count), .Q(counter_1_q), .clk(CLK), .clr(or_3_out));  // open: carry
  or or_3 (or_3_out, ~Chip_Select, Reset);  // OR_Gate
  Comparator #(.width(4), .mode("unsigned")) comparator_1 (
    .a(4'b0000), .b(counter_1_q), .eq(Zero_Time));  // open: gt, lt
  or or_4 (or_4_out, Count, Load0, Load1);
  Register #(.width(32)) register_1 (.D(Data_In_0), .en(Chip_Select), .Q(register_1_q), .clk(CLK), .clr(or_5_out));
  or or_5 (or_5_out, ~Chip_Select, Reset);  // OR_Gate
  Register #(.width(32)) register_2 (.D(Data_In_1), .en(Chip_Select), .Q(register_2_q), .clk(CLK), .clr(or_6_out));
  or or_6 (or_6_out, ~Chip_Select, Reset);  // OR_Gate
  Register #(.width(32)) register_3 (.D(Data_In_2), .en(Chip_Select), .Q(register_3_q), .clk(CLK), .clr(or_7_out));
  or or_7 (or_7_out, ~Chip_Select, Reset);  // OR_Gate
  Register #(.width(32)) register_4 (.D(Data_In_3), .en(Chip_Select), .Q(register_4_q), .clk(CLK), .clr(or_8_out));
  or or_8 (or_8_out, ~Chip_Select, Reset);  // OR_Gate
  Register #(.width(32)) register_5 (
    .D({{11{1'b1}}, nRead_Write, Mask, Address}), .en(Chip_Select), .Q(register_5_q), .clk(CLK),
    .clr(or_9_out));
  or or_9 (or_9_out, ~Chip_Select, Reset);  // OR_Gate
  D_Flip_Flop Proc (.clk(CLK), .D(or_4_out), .Q(Proc_q), .reset(or_10_out));  // open: Qn, preset, en
  or or_10 (or_10_out, ~Chip_Select, Reset);  // OR_Gate
  Demultiplexer #(.enable("false")) demultiplexer_2 (
    .out0(Count), .out1(Update_Mem), .in(demultiplexer_3_out0), .sel(Zero_Time));
  Demultiplexer #(.enable("false")) demultiplexer_3 (
    .out0(demultiplexer_3_out0), .out1(Load1), .in(Proc_q), .sel(Changed));
  Clock clock_1 (.out(CLK));
  Comparator #(.width(32)) comparator_2 (.a(register_1_q), .b(Data_In_0), .eq(comparator_2_eq));  // open: gt, lt
  Comparator #(.width(32)) comparator_3 (.a(register_2_q), .b(Data_In_1), .eq(comparator_3_eq));  // open: gt, lt
  Comparator #(.width(32)) comparator_4 (.a(register_3_q), .b(Data_In_2), .eq(comparator_4_eq));  // open: gt, lt
  Comparator #(.width(32)) comparator_5 (.a(register_4_q), .b(Data_In_3), .eq(comparator_5_eq));  // open: gt, lt
  Comparator #(.width(32)) comparator_6 (
    .a(register_5_q), .b({{11{1'b1}}, nRead_Write, Mask, Address}), .eq(comparator_6_eq));  // open: gt, lt
  nand nand_1 (nand_1_out, comparator_6_eq, comparator_2_eq, comparator_3_eq, comparator_4_eq, comparator_5_eq);
  and and_1 (Changed, nand_1_out, Chip_Select);
  or or_11 (Load, Count, Load1, Load0);
  and and_2 (and_2_out, Mask[0], Update_Mem, nRead_Write);
  and and_3 (and_3_out, Mask[1], Update_Mem, nRead_Write);
  and and_4 (and_4_out, Mask[2], Update_Mem, nRead_Write);
  and and_5 (and_5_out, Mask[3], Update_Mem, nRead_Write);
  RAM_part #(.addrWidth(16), .dataWidth(32), .bus("separate")) ram_1 (
    .addr(Address), .din(Data_In_0), .data(Data_Out_0), .str(and_2_out), .sel(Chip_Select), .clk(CLK),
    .ld(and_6_out), .clr(Reset));
  and and_6 (and_6_out, ~nRead_Write, Idle);  // AND_Gate
  RAM_part #(.addrWidth(16), .dataWidth(32), .bus("separate")) ram_2 (
    .addr(Address), .din(Data_In_1), .data(Data_Out_1), .str(and_3_out), .sel(Chip_Select), .clk(CLK),
    .ld(and_7_out), .clr(Reset));
  and and_7 (and_7_out, ~nRead_Write, Idle);  // AND_Gate
  RAM_part #(.addrWidth(16), .dataWidth(32), .bus("separate")) ram_3 (
    .addr(Address), .din(Data_In_2), .data(Data_Out_2), .str(and_4_out), .sel(Chip_Select), .clk(CLK),
    .ld(and_8_out), .clr(Reset));
  and and_8 (and_8_out, ~nRead_Write, Idle);  // AND_Gate
  RAM_part #(.addrWidth(16), .dataWidth(32), .bus("separate")) ram_4 (
    .addr(Address), .din(Data_In_3), .data(Data_Out_3), .str(and_5_out), .sel(Chip_Select), .clk(CLK),
    .ld(and_9_out), .clr(Reset));
  and and_9 (and_9_out, ~nRead_Write, Idle);  // AND_Gate

  assign Read_Time = 4'b0011;
  assign Write_Time = 4'b0010;

  // Other names for the same wires on the sheet: M0 = Mask[0]; M1 = Mask[1]; M2 = Mask[2]; M3 = Mask[3];
  //   RW = nRead_Write; CLR = Reset; CS = Chip_Select; Load2 = Count

  // Notes on the sheet:
  //   NO MODIFICAR
  //   excepto quizás los valores RT y WT
  //   BANK0
  //   BANK1
  //   BANK2
  //   BANK3
endmodule

module S_MIPS (
  input  Kbd_Available,
  input  [6:0] Kbd_ASCII_Data,
  input  [31:0] RAM_Out_0,
  input  [31:0] RAM_Out_1,
  input  Reset,
  input  [31:0] RAM_Out_2,
  input  Clock,
  input  [31:0] RAM_Out_3,
  input  [3:0] Read_Time,
  input  [3:0] Write_Time,
  output Kbd_Enable,
  output [15:0] Address,
  output Kbd_Clear,
  output TTY_Enable,
  output [6:0] TTY_ASCII_Data,
  output Stop,
  output [31:0] RAM_In_0,
  output [31:0] RAM_In_1,
  output [31:0] RAM_In_2,
  output [31:0] RAM_In_3,
  output [3:0] Mask,
  output nRead_Write,
  output Chip_Select
);


  // Other names for the same wires on the sheet: CLK = Clock; CLR = Reset; CS = Chip_Select;
  //   KBD_AVAIL = Kbd_Available; KBD_CLR = Kbd_Clear; KBD_DATA[6:0] = Kbd_ASCII_Data; RAM_A[15:0] = Address;
  //   RAM_INPUT_0[31:0] = RAM_In_0; RAM_INPUT_1[31:0] = RAM_In_1; RAM_INPUT_2[31:0] = RAM_In_2;
  //   RAM_INPUT_3[31:0] = RAM_In_3; RAM_MASK[3:0] = Mask; RAM_OUTPUT_0[31:0] = RAM_Out_0;
  //   RAM_OUTPUT_1[31:0] = RAM_Out_1; RAM_OUTPUT_2[31:0] = RAM_Out_2; RAM_OUTPUT_3[31:0] = RAM_Out_3;
  //   RW = nRead_Write; TTY_DATA[6:0] = TTY_ASCII_Data

  // Notes on the sheet:
  //   RAM ADDRESS
  //   DATA FROM RAM
  //   DATA TO RAM
  //   DATA WRITE MASK
  //   RAM TIMING
  //   RAM CONTROL
  //   KEYBOARD
  //   TTY
  //   SEQUENCING
endmodule

module RAM_Dispatcher (
  input  [3:0] WriteTime,
  input  Clock,
  input  CLR,
  output [31:0] Data,
  output [15:0] Address,
  output [3:0] Mask,
  output Finished,
  output Write
);

  wire demultiplexer_2_out1, demultiplexer_3_out1, End, IDLE_q, IncAddr, Load, or_1_out, or_2_out, While_q,
       WriteEnd;
  wire [3:0] counter_1_q;
  wire [31:0] CurrentAddress_q;

  Counter #(.width(32), .max('hffffffff)) CurrentAddress (
    .count(IncAddr), .Q({CurrentAddress_q[31:18], Address, CurrentAddress_q[1:0]}), .clk(Clock), .clr(CLR));  // open: load, D, carry
  or or_1 (or_1_out, IncAddr, demultiplexer_3_out1, Finished);
  D_Flip_Flop IDLE (.clk(Clock), .D(or_1_out), .Q(IDLE_q), .preset(CLR));  // open: Qn, en, reset
  Demultiplexer #(.enable("false")) demultiplexer_1 (.out0(Load), .out1(Finished), .in(IDLE_q), .sel(End));
  D_Flip_Flop While (.clk(Clock), .D(or_2_out), .Q(While_q), .reset(CLR));  // open: Qn, preset, en
  or or_2 (or_2_out, Write, Load);
  RAM_part #(.addrWidth(18), .dataWidth(32)) ram_1 (
    .addr({Address, CurrentAddress_q[1:0]}), .data(Data), .clk(Clock));  // open: sel, ld, clr
  Demultiplexer #(.enable("false")) demultiplexer_2 (
    .out0(Write), .out1(demultiplexer_2_out1), .in(While_q), .sel(WriteEnd));
  Decoder #(.select(2)) decoder_1 (
    .out0(Mask[0]), .out1(Mask[1]), .out2(Mask[2]), .out3(Mask[3]), .sel(CurrentAddress_q[1:0]));  // open: en
  Demultiplexer #(.enable("false")) demultiplexer_3 (
    .out0(IncAddr), .out1(demultiplexer_3_out1), .in(demultiplexer_2_out1), .sel(End));
  Counter #(.width(4), .max('hf)) counter_1 (
    .load(Load), .D(WriteTime), .count(Write), .Q(counter_1_q), .clk(Clock));  // open: carry, clr
  Comparator #(.width(32)) comparator_1 (.a(Data), .b({32{1'b1}}), .eq(End));  // open: gt, lt
  Comparator #(.width(4)) comparator_2 (.a(4'b0000), .b(counter_1_q), .eq(WriteEnd));  // open: gt, lt

  // Other names for the same wires on the sheet: CLK = Clock; Count = Write; WT[3:0] = WriteTime
endmodule

module DataPath_2 (
  input  [3:0] Operation_Selector,
  input  W_HI_LO,
  input  CLK,
  input  W_RF,
  input  RST_RF,
  input  DA_SEL,
  input  [31:0] Data_From_Ram,
  input  [2:0] DI_SEL,
  input  [1:0] PC_Selector,
  input  LD_PC,
  input  [2:0] Branch_Selector,
  input  LD_IR,
  input  [31:0] Instruction,
  input  [1:0] Addres_Sel,
  input  Data_Sel,
  input  LD_SP,
  input  Operand_Selector_A,
  input  [1:0] Operand_Selector_B,
  input  KBD_AVAIBLE,
  input  [6:0] KBD_DATA,
  output [5:0] funccode,
  output [5:0] opcode,
  output [31:0] RAM_Address,
  output [31:0] Data_to_RAM,
  output [6:0] TTY_DATA
);

  wire SF, ZF;
  wire [4:0] multiplexer_3_out, rd, rs, rt;
  wire [15:0] inm;
  wire [25:0] Label;
  wire [31:0] ALU_RESULT, B, bit_extender_1_out, bit_extender_2_out, bit_extender_3_out,
       branch_control_1_pc_prime, HI, IHI, ILO, IR_q, LO, multiplexer_1_out, multiplexer_2_out,
       multiplexer_4_out, multiplexer_5_out, PC, Random_out, SP;
  wire [31:7] A;

  Random #(.width(32)) Random (.clk(CLK), .next(1'b1), .out(Random_out));  // open: clr
  assign bit_extender_1_out = {{25{1'b0}}, KBD_DATA};  // Bit_Extender bit_extender_1
  Multiplexer #(.width(32), .enable("false")) multiplexer_1 (
    .in0(bit_extender_1_out), .in1({32{1'b1}}), .out(multiplexer_1_out), .sel(KBD_AVAIBLE));
  Register #(.width(32)) IR (.D(Instruction), .en(LD_IR), .Q(IR_q), .clk(CLK));  // open: clr
  Multiplexer #(.select(3), .width(32), .enable("false")) multiplexer_2 (
    .in0(ALU_RESULT), .in1(HI), .in2(LO), .in3(Data_From_Ram), .in4(Random_out), .in5(multiplexer_1_out),
    .out(multiplexer_2_out), .sel(DI_SEL));  // open: in6, in7
  Multiplexer #(.width(5), .enable("false")) multiplexer_3 (.in0(rd), .in1(rt), .out(multiplexer_3_out), .sel(DA_SEL));
  InstructionSplitter instructionsplitter_1 (
    .Input(IR_q), .func(funccode), .rd(rd), .rt(rt), .rs(rs), .Opcode(opcode), .Inmediato(inm), .Jump(Label));  // open: shamt
  RegisterFile registerfile_1 (
    .DA(multiplexer_3_out), .DI(multiplexer_2_out), .RW(W_RF), .Rst(RST_RF), .CLK(CLK), .SA(rs), .SB(rt),
    .A({A, TTY_DATA}), .B(B), .Right_Hi___Low(W_HI_LO), .Low(LO), .Hi(HI), .Stack_Pointer(SP),
    .In_SP(ALU_RESULT), .Ld_SP(LD_SP), .In_Hi(IHI), .In_Low(ILO));
  Branch_Control branch_control_1 (
    .Destiny(Label), .Program_Counter(PC), .PC_selector(PC_Selector), .SF(SF), .RS({A, TTY_DATA}), .ZF(ZF),
    .Inmediate_Constant(inm), .Branch_Selector(Branch_Selector), .PC_prime(branch_control_1_pc_prime));
  assign bit_extender_2_out = {{16{1'b0}}, inm};  // Bit_Extender bit_extender_2
  assign bit_extender_3_out = {{16{inm[15]}}, inm};  // Bit_Extender bit_extender_3
  ProgramCounter programcounter_1 (.In(branch_control_1_pc_prime), .En_PC(LD_PC), .clock(CLK), .Output(PC));
  Multiplexer #(.width(32), .enable("false")) multiplexer_4 (
    .in0({A, TTY_DATA}), .in1(SP), .out(multiplexer_4_out), .sel(Operand_Selector_A));
  Multiplexer #(.select(2), .width(32), .enable("false")) multiplexer_5 (
    .in0(B), .in1(32'h4), .in2(bit_extender_2_out), .in3(bit_extender_3_out), .out(multiplexer_5_out),
    .sel(Operand_Selector_B));
  ALU alu_1 (
    .OP(Operation_Selector), .Result(ALU_RESULT), .Hi(IHI), .Lo(ILO), .In1(multiplexer_4_out),
    .In2(multiplexer_5_out), .Negative(SF), .Zero(ZF));
  Multiplexer #(.select(2), .width(32), .enable("false")) multiplexer_6 (
    .in0(ALU_RESULT), .in1(PC), .in2({A, TTY_DATA}), .in3(SP), .out(RAM_Address), .sel(Addres_Sel));
  Multiplexer #(.width(32), .enable("false")) multiplexer_7 (
    .in0({A, TTY_DATA}), .in1(B), .out(Data_to_RAM), .sel(Data_Sel));

  // Other names for the same wires on the sheet: A[6:0] = TTY_DATA; BRCH_SEL[2:0] = Branch_Selector;
  //   OPERATION_SEL[3:0] = Operation_Selector; PC_SEL[1:0] = PC_Selector

  // Notes on the sheet:
  //   Inputs
  //   Instruction Splitter
  //   ALU && RF
  //   BranchControl && PC
  //   Out
endmodule

module ALU (
  input  [31:0] In1,
  input  [31:0] In2,
  input  [3:0] OP,
  output Negative,
  output Zero,
  output [31:0] Result,
  output [31:0] Hi,
  output [31:0] Lo
);

  wire _1_1, _1_2, _2_1, _2_2, addc, comparator_1_lt, comparator_2_lt, subc;
  wire [31:0] add, \and , divHi, divLo, divuHi, divuLo, mulHi, mulLo, muluHi, muluLo, \nor , \not , \or ,
       slt, sltu, sub, \xor ;

  Demultiplexer #(.enable("false")) demultiplexer_1 (.out0(_1_1), .out1(_2_1), .in(OP[0]), .sel(OP[3]));
  Demultiplexer #(.enable("false")) demultiplexer_2 (.out0(_1_2), .out1(_2_2), .in(OP[1]), .sel(OP[3]));
  Adder #(.width(32)) adder_1 (.a(In1), .b(In2), .out(add), .cout(addc));  // open: cin
  Subtractor #(.width(32)) subtractor_1 (.a(In1), .b(In2), .out(sub), .bout(subc));  // open: bin
  SignedDivider SignDiv (.x(In1), .y(In2), .DivRem(divLo), .Div(divHi));
  Divider #(.width(32)) divider_1 (.a(In1), .b(In2), .out(divuLo), .rem(divuHi));  // open: upper
  Multiplier #(.width(32)) multiplier_1 (.a(In1), .b(In2), .out(mulLo), .cout(mulHi));  // open: cin
  SignedMultiplier SignMult (.In1(In1), .In2(In2), .Lo(muluLo), .Hi(muluHi));
  Comparator #(.width(32), .mode("unsigned")) comparator_1 (.a(In1), .b(In2), .lt(comparator_1_lt));  // open: gt, eq
  Comparator #(.width(32)) comparator_2 (.a(In1), .b(In2), .lt(comparator_2_lt));  // open: gt, eq
  assign \and  = In1 & In2;  // AND_Gate and_1, 32 bits wide
  assign \xor  = In1 ^ In2;  // XOR_Gate xor_1, 32 bits wide
  assign \or  = In1 | In2;  // OR_Gate or_1, 32 bits wide
  Multiplexer #(.width(32), .enable("false")) multiplexer_1 (
    .in0({32{1'b0}}), .in1(32'h1), .out(sltu), .sel(comparator_1_lt));
  Multiplexer #(.width(32), .enable("false")) multiplexer_2 (
    .in0({32{1'b0}}), .in1(32'h1), .out(slt), .sel(comparator_2_lt));
  assign \nor  = ~(In1 | In2);  // NOR_Gate nor_1, 32 bits wide
  assign \not  = ~In1;  // NOT_Gate not_1, 32 bits wide
  Comparator #(.width(32)) comparator_3 (.a({32{1'b0}}), .b({Negative, Result[30:0]}), .eq(Zero));  // open: gt, lt
  Multiplexer #(.select(3), .width(32), .enable("false")) multiplexer_3 (
    .in0(add), .in1(sub), .in2(slt), .in3(sltu), .in4(\xor ), .in5(\or ), .in6(\and ), .in7(\nor ),
    .out({Negative, Result[30:0]}), .sel({OP[2], _1_2, _1_1}));
  Multiplexer #(.select(2), .width(32)) multiplexer_4 (
    .in0(mulHi), .in1(muluHi), .in2(divHi), .in3(divuHi), .out(Hi), .sel({_2_2, _2_1}), .en(OP[3]));
  Multiplexer #(.select(2), .width(32)) multiplexer_5 (
    .in0(mulLo), .in1(muluLo), .in2(divLo), .in3(divuLo), .out(Lo), .sel({_2_2, _2_1}), .en(OP[3]));

  assign Result[31] = Negative;

  // Other names for the same wires on the sheet: Op_2 = OP[3]; Selector_1[2:0] = {OP[2], _1_2, _1_1}; _1_3 = OP[2];
  //   Selector_2[1:0] = {_2_2, _2_1}

  // Notes on the sheet:
  //   Inputs:
  //   Separate Operation:
  //   Arithmetic Logic Unit:
  //   Aritmetic Operators:
  //   Set less than: sltu
  //   Set less than signed: slt
  //   Logic Operators:
  //   Flags:
  //   Results:
endmodule

module SignedMultiplier (
  input  [31:0] In1,
  input  [31:0] In2,
  output [31:0] Lo,
  output [31:0] Hi
);

  wire adder_1_cout, adder_3_cout;
  wire [15:0] mix1_high, mix1_low, mix2_high, mix2_low;
  wire [31:0] adder_1_out, adder_2_out, bit_extender_5_out, bit_extender_6_out, prehigh, prelower, value_1_0,
       value_1_1, value_2_0, value_2_1;

  assign value_1_0 = {{16{1'b0}}, In1[15:0]};  // Bit_Extender bit_extender_1
  assign value_1_1 = {{16{1'b0}}, In1[31:16]};  // Bit_Extender bit_extender_2
  assign value_2_0 = {{16{1'b0}}, In2[15:0]};  // Bit_Extender bit_extender_3
  assign value_2_1 = {{16{1'b0}}, In2[31:16]};  // Bit_Extender bit_extender_4
  Multiplier #(.width(32)) multiplier_1 (.a(value_1_0), .b(value_2_0), .out(prelower));  // open: cin, cout
  Multiplier #(.width(32)) multiplier_2 (.a(value_1_0), .b(value_2_1), .out({mix1_high, mix1_low}));  // open: cin, cout
  Multiplier #(.width(32)) multiplier_3 (.a(value_1_1), .b(value_2_0), .out({mix2_high, mix2_low}));  // open: cin, cout
  Multiplier #(.width(32)) multiplier_4 (.a(value_1_1), .b(value_2_1), .out(prehigh));  // open: cin, cout
  assign bit_extender_5_out = {{16{1'b0}}, mix1_high};  // Bit_Extender bit_extender_5
  assign bit_extender_6_out = {{16{1'b0}}, mix2_high};  // Bit_Extender bit_extender_6
  Adder #(.width(32)) adder_1 (
    .a({mix1_low, {16{1'b0}}}), .b({mix2_low, {16{1'b0}}}), .out(adder_1_out), .cout(adder_1_cout));  // open: cin
  Adder #(.width(32)) adder_2 (
    .a(bit_extender_5_out), .b(bit_extender_6_out), .out(adder_2_out), .cin(adder_1_cout));  // open: cout
  Adder #(.width(32)) adder_3 (.a(prelower), .b(adder_1_out), .out(Lo), .cout(adder_3_cout));  // open: cin
  Adder #(.width(32)) adder_4 (.a(prehigh), .b(adder_2_out), .out(Hi), .cin(adder_3_cout));  // open: cout
endmodule

module SignedDivider (
  input  [31:0] x,
  input  [31:0] y,
  output [31:0] DivRem,
  output [31:0] Div
);

  wire SignX, SignY, xor_1_out;
  wire [31:0] adder_1_out, Div_t, multiplexer_3_out, negator_1_out, negator_2_out, negator_3_out, Rem,
       subtractor_1_out, X1, Y1;

  Sign sign_1 (.X(x), .Sign(SignX));
  Sign sign_2 (.X(y), .Sign(SignY));
  Negator #(.width(32)) negator_1 (.in(x), .out(negator_1_out));
  Negator #(.width(32)) negator_2 (.in(y), .out(negator_2_out));
  Multiplexer #(.width(32), .enable("false")) multiplexer_1 (.in0(x), .in1(negator_1_out), .out(X1), .sel(SignX));
  Multiplexer #(.width(32), .enable("false")) multiplexer_2 (.in0(y), .in1(negator_2_out), .out(Y1), .sel(SignY));
  Divider #(.width(32)) divider_1 (.a(X1), .b(Y1), .out(Div_t), .rem(Rem));  // open: upper
  Adder #(.width(32)) adder_1 (.a(Div_t), .b(32'h1), .out(adder_1_out));  // open: cin, cout
  Multiplexer #(.width(32), .enable("false")) multiplexer_3 (
    .in0(Div_t), .in1(adder_1_out), .out(multiplexer_3_out), .sel(SignX));
  Subtractor #(.width(32)) subtractor_1 (.a(Y1), .b(Rem), .out(subtractor_1_out));  // open: bin, bout
  Negator #(.width(32)) negator_3 (.in(multiplexer_3_out), .out(negator_3_out));
  Multiplexer #(.width(32)) multiplexer_4 (.in0(Rem), .in1(subtractor_1_out), .out(DivRem), .sel(SignX));  // open: en
  Multiplexer #(.width(32), .enable("false")) multiplexer_5 (
    .in0(multiplexer_3_out), .in1(negator_3_out), .out(Div), .sel(xor_1_out));
  xor xor_1 (xor_1_out, SignY, SignX);

  // Other names for the same wires on the sheet: OH[31:0] = DivRem; OL[31:0] = Div
endmodule

module Sign (
  input  [31:0] X,
  output Sign
);


  assign Sign = X[31];
endmodule

module ProgramCounter (
  input  [31:0] In,
  input  En_PC,
  input  clock,
  output [31:0] Output
);

  Register #(.width(32)) register_1 (.D(In), .en(En_PC), .Q(Output), .clk(clock));  // open: clr

  // Other names for the same wires on the sheet: clk = clock; En = En_PC; Ou[31:0] = Output

  // Notes on the sheet:
  //   Inputs:
  //   Register:
  //   Program Counter:
  //   Output:
endmodule

module InstructionSplitter (
  input  [31:0] Input,
  output [5:0] func,
  output [4:0] shamt,
  output [4:0] rd,
  output [4:0] rt,
  output [4:0] rs,
  output [5:0] Opcode,
  output [15:0] Inmediato,
  output [25:0] Jump
);


  assign func = Input[5:0];
  assign Inmediato = Input[15:0];
  assign Jump = Input[25:0];
  assign Opcode = Input[31:26];
  assign rd = Input[15:11];
  assign rs = Input[25:21];
  assign rt = Input[20:16];
  assign shamt = Input[10:6];

  // Notes on the sheet:
  //   Inmediato: pull=down
endmodule

module InstructionDecoder (
  input  [31:0] Instruction_In,
  input  Clock,
  output Enable_Hi_Lo,
  output [4:0] Register_B_Selector,
  output [4:0] Register_A_Selector,
  output [4:0] Selector_of_the_register_to_write,
  output [31:0] Constant_k,
  output [25:0] destination_jmp,
  output [3:0] Operation_ALU,
  output [2:0] Data_Input_Selector,
  output Compare_to_Zero_Enable,
  output [1:0] Compare_to_Zero_Selector,
  output Compare_to_other_register_Enable,
  output Compare_to_other_register_Selector,
  output jmp__Instruccion_de_Salto_con_Constante,
  output jr__Instruccion_de_Salto_con_Registro,
  output Inmediate_operation_enable,
  output pop,
  output push,
  output halt__Stop_program,
  output tty__Write_to_terminal,
  output lw__load_word,
  output sw__store_word,
  output [2:0] Operation_Type
);

  wire _000_000, _111_000, _111_111, add, addi, ALU_En, \and , andi, BF, bgtz, blez, bltz, bne, DI_En, div,
       divu, En_1, F_add, F_and, F_nor, F_or, F_slt, F_sltu, F_sub, F_xor, jump_t, k_En, kbd, mfhi, mflo,
       mult, mulu, nop, \or , or_2_out, or_3_out, or_16_out, or_19_out, or_20_out, ori, rnd, slt, slti,
       sltiu, sltu, Spliter_0, Spliter_1, SRI, word_inst, write_inst, \xor , xori;
  wire [1:0] k_selector;
  wire [4:0] rd, rs, rt;
  wire [5:0] Funcode, Opcode;
  wire [15:0] Constant;
  wire [29:0] bit_extender_1_out;
  wire [31:0] bit_extender_2_out, bit_extender_3_out, random_1_out;

  // InstructionSplitter instructionsplitter_1: pin names not known; wires that end beside it: Instruction_In, Funcode, rd, rt, rs, Opcode, Constant, destination_jmp
  and and_1 (add, _000_000, Funcode[5], ~Funcode[4], ~Funcode[3], ~Funcode[2], ~Funcode[1], ~Funcode[0]);  // AND_Gate
  and and_2 (slt, _000_000, Funcode[5], ~Funcode[4], Funcode[3], ~Funcode[2], Funcode[1], ~Funcode[0]);  // AND_Gate
  and and_3 (\xor , _000_000, Funcode[5], ~Funcode[4], Funcode[3], ~Funcode[2], ~Funcode[1], ~Funcode[0]);  // AND_Gate
  and and_4 (\and , _000_000, Funcode[5], ~Funcode[4], ~Funcode[3], Funcode[2], ~Funcode[1], ~Funcode[0]);  // AND_Gate
  and and_5 (mult, _000_000, ~Funcode[5], Funcode[4], Funcode[3], ~Funcode[2], ~Funcode[1], ~Funcode[0]);  // AND_Gate
  and and_6 (div, _000_000, ~Funcode[5], Funcode[4], Funcode[3], ~Funcode[2], Funcode[1], ~Funcode[0]);  // AND_Gate
  or or_1 (En_1, _000_000, _111_000);
  and and_7 (_000_000, ~Opcode[5], ~Opcode[4], ~Opcode[3], ~Opcode[2], ~Opcode[1], ~Opcode[0]);  // AND_Gate
  assign Register_A_Selector = En_1 ? rs : 5'bz;  // Controlled_Buffer controlled_buffer_1
  assign Register_B_Selector = En_1 ? rt : 5'bz;  // Controlled_Buffer controlled_buffer_2
  and and_8 (F_sub, _000_000, Funcode[5], ~Funcode[4], ~Funcode[3], ~Funcode[2], Funcode[1], ~Funcode[0]);  // AND_Gate
  and and_9 (sltu, _000_000, Funcode[5], ~Funcode[4], Funcode[3], ~Funcode[2], Funcode[1], Funcode[0]);  // AND_Gate
  and and_10 (\or , _000_000, Funcode[5], ~Funcode[4], ~Funcode[3], Funcode[2], ~Funcode[1], Funcode[0]);  // AND_Gate
  and and_11 (F_nor, _000_000, Funcode[5], ~Funcode[4], ~Funcode[3], Funcode[2], Funcode[1], Funcode[0]);  // AND_Gate
  and and_12 (mulu, _000_000, ~Funcode[5], Funcode[4], Funcode[3], ~Funcode[2], ~Funcode[1], Funcode[0]);  // AND_Gate
  and and_13 (divu, _000_000, ~Funcode[5], Funcode[4], Funcode[3], ~Funcode[2], Funcode[1], Funcode[0]);  // AND_Gate
  assign Selector_of_the_register_to_write = En_1 ? rd : 5'bz;  // Controlled_Buffer controlled_buffer_3
  and and_14 (_111_000, Opcode[5], Opcode[4], Opcode[3], ~Opcode[2], ~Opcode[1], ~Opcode[0]);  // AND_Gate
  and and_15 (nop, _000_000, ~Funcode[5], ~Funcode[4], ~Funcode[3], ~Funcode[2], ~Funcode[1], ~Funcode[0]);  // AND_Gate
  and and_16 (mfhi, _000_000, ~Funcode[5], Funcode[4], ~Funcode[3], ~Funcode[2], ~Funcode[1], ~Funcode[0]);  // AND_Gate
  and and_17 (pop, _111_000, ~Funcode[5], ~Funcode[4], ~Funcode[3], ~Funcode[2], ~Funcode[1], ~Funcode[0]);  // AND_Gate
  and and_18 (halt__Stop_program, _111_111, Funcode[5], Funcode[4], Funcode[3], Funcode[2], Funcode[1], Funcode[0]);
  and and_19 (rnd, _111_111, ~Funcode[5], ~Funcode[4], ~Funcode[3], ~Funcode[2], Funcode[1], ~Funcode[0]);  // AND_Gate
  assign Register_A_Selector = tty__Write_to_terminal ? rs : 5'bz;  // Controlled_Buffer controlled_buffer_4
  and and_20 (_111_111, Opcode[5], Opcode[4], Opcode[3], Opcode[2], Opcode[1], Opcode[0]);
  assign Selector_of_the_register_to_write = or_2_out ? rd : 5'bz;  // Controlled_Buffer controlled_buffer_5
  or or_2 (or_2_out, kbd, rnd);
  and and_21 (jr__Instruccion_de_Salto_con_Registro, _000_000, ~Funcode[5], ~Funcode[4], Funcode[3], ~Funcode[2], ~Funcode[1], ~Funcode[0]);  // AND_Gate
  and and_22 (mflo, _000_000, ~Funcode[5], Funcode[4], ~Funcode[3], ~Funcode[2], Funcode[1], ~Funcode[0]);  // AND_Gate
  and and_23 (push, _111_000, ~Funcode[5], ~Funcode[4], ~Funcode[3], ~Funcode[2], ~Funcode[1], Funcode[0]);  // AND_Gate
  and and_24 (tty__Write_to_terminal, _111_111, ~Funcode[5], ~Funcode[4], ~Funcode[3], ~Funcode[2], ~Funcode[1], Funcode[0]);  // AND_Gate
  and and_25 (kbd, _111_111, ~Funcode[5], ~Funcode[4], ~Funcode[3], Funcode[2], ~Funcode[1], ~Funcode[0]);  // AND_Gate
  or or_3 (or_3_out, pop, lw__load_word);
  Priority_Encoder priority_encoder_1 (
    .in0(ALU_En), .in1(mfhi), .in2(mflo), .in3(kbd), .in4(rnd), .in5(or_3_out), .out(Data_Input_Selector),
    .gs(DI_En));  // open: in6, in7, en_in, en_out
  or or_4 (Enable_Hi_Lo, mult, mulu, div, divu);
  and and_26 (addi, ~Opcode[5], ~Opcode[4], Opcode[3], ~Opcode[2], ~Opcode[1], ~Opcode[0]);  // AND_Gate
  and and_27 (andi, ~Opcode[5], ~Opcode[4], Opcode[3], Opcode[2], ~Opcode[1], ~Opcode[0]);  // AND_Gate
  and and_28 (bgtz, ~Opcode[5], ~Opcode[4], ~Opcode[3], Opcode[2], Opcode[1], Opcode[0]);  // AND_Gate
  and and_29 (blez, ~Opcode[5], ~Opcode[4], ~Opcode[3], Opcode[2], Opcode[1], ~Opcode[0]);  // AND_Gate
  or or_5 (Spliter_0, addi, ori, sltiu, lw__load_word, andi, xori, slti);
  assign Register_A_Selector = Spliter_0 ? rs : 5'bz;  // Controlled_Buffer controlled_buffer_6
  assign Selector_of_the_register_to_write = Spliter_0 ? rt : 5'bz;  // Controlled_Buffer controlled_buffer_7
  and and_30 (lw__load_word, Opcode[5], ~Opcode[4], ~Opcode[3], ~Opcode[2], Opcode[1], Opcode[0]);  // AND_Gate
  and and_31 (slti, ~Opcode[5], ~Opcode[4], Opcode[3], ~Opcode[2], Opcode[1], ~Opcode[0]);  // AND_Gate
  and and_32 (sltiu, ~Opcode[5], ~Opcode[4], Opcode[3], ~Opcode[2], Opcode[1], Opcode[0]);  // AND_Gate
  and and_33 (bne, ~Opcode[5], ~Opcode[4], ~Opcode[3], Opcode[2], ~Opcode[1], Opcode[0]);  // AND_Gate
  and and_34 (Compare_to_other_register_Selector, ~Opcode[5], ~Opcode[4], ~Opcode[3], Opcode[2], ~Opcode[1], ~Opcode[0]);  // AND_Gate
  assign Register_A_Selector = Spliter_1 ? rs : 5'bz;  // Controlled_Buffer controlled_buffer_8
  and and_35 (sw__store_word, Opcode[5], ~Opcode[4], Opcode[3], ~Opcode[2], Opcode[1], Opcode[0]);  // AND_Gate
  or or_6 (Spliter_1, BF, sw__store_word);
  assign Register_B_Selector = Spliter_1 ? rt : 5'bz;  // Controlled_Buffer controlled_buffer_9
  and and_36 (xori, ~Opcode[5], ~Opcode[4], Opcode[3], Opcode[2], Opcode[1], ~Opcode[0]);  // AND_Gate
  and and_37 (ori, ~Opcode[5], ~Opcode[4], Opcode[3], Opcode[2], ~Opcode[1], Opcode[0]);  // AND_Gate
  and and_38 (bltz, ~Opcode[5], ~Opcode[4], ~Opcode[3], ~Opcode[2], ~Opcode[1], Opcode[0]);  // AND_Gate
  assign Selector_of_the_register_to_write = Spliter_1 ? {5{1'b0}} : 5'bz;  // Controlled_Buffer controlled_buffer_10
  or or_7 (BF, Compare_to_other_register_Selector, blez, bltz, bne, bgtz);
  or or_8 (Compare_to_other_register_Enable, bne, Compare_to_other_register_Selector);
  Priority_Encoder #(.select(2)) priority_encoder_2 (
    .in1(bgtz), .in2(blez), .in3(bltz), .out(Compare_to_Zero_Selector), .gs(Compare_to_Zero_Enable));  // open: in0, en_out, en_in
  or or_9 (Inmediate_operation_enable, lw__load_word, slti, sltiu, ori, kbd, addi, andi, xori, sw__store_word);
  or or_10 (F_add, add, kbd, addi, lw__load_word, sw__store_word);
  or or_11 (F_sltu, sltu, sltiu);
  or or_12 (F_or, \or , ori);
  and and_39 (jmp__Instruccion_de_Salto_con_Constante, ~Opcode[5], ~Opcode[4], ~Opcode[3], ~Opcode[2], Opcode[1], ~Opcode[0]);  // AND_Gate
  Priority_Encoder #(.select(4)) priority_encoder_3 (
    .in0(F_add), .in1(F_sub), .in2(F_slt), .in3(F_sltu), .in4(F_xor), .in5(F_or), .in6(F_and), .in7(F_nor),
    .in8(mult), .in9(mulu), .in10(div), .in11(divu), .out(Operation_ALU), .gs(ALU_En));  // open: in12, in13, in14, in15, en_out, en_in
  or or_13 (F_xor, \xor , xori);
  or or_14 (F_slt, slt, slti);
  or or_15 (F_and, \and , andi);
  or or_16 (or_16_out, ALU_En, SRI);
  or or_17 (SRI, rnd, mfhi, mflo, kbd);
  or or_18 (jump_t, BF, jr__Instruccion_de_Salto_con_Registro, jmp__Instruccion_de_Salto_con_Constante, nop);
  or or_19 (or_19_out, sltiu, slti, lw__load_word, addi, sw__store_word);
  or or_20 (or_20_out, xori, andi, ori);
  assign bit_extender_1_out = {{14{Constant[15]}}, Constant};  // Bit_Extender bit_extender_1
  Random #(.width(32)) random_1 (.clk(Clock), .next(rnd), .out(random_1_out));  // open: clr
  Priority_Encoder #(.select(2)) priority_encoder_4 (
    .in0(BF), .in1(or_19_out), .in2(or_20_out), .in3(rnd), .out(k_selector), .gs(k_En));  // open: en_out, en_in
  assign bit_extender_2_out = {{16{Constant[15]}}, Constant};  // Bit_Extender bit_extender_2
  assign bit_extender_3_out = {{16{1'b0}}, Constant};  // Bit_Extender bit_extender_3
  Priority_Encoder priority_encoder_5 (
    .in0(halt__Stop_program), .in1(or_16_out), .in3(word_inst), .in4(tty__Write_to_terminal),
    .in6(write_inst), .in7(jump_t), .out(Operation_Type));  // open: in2, in5, en_in, gs, en_out
  or or_21 (word_inst, pop, lw__load_word);
  or or_22 (write_inst, sw__store_word, push);
  Multiplexer #(.select(2), .width(32)) multiplexer_1 (
    .in0({bit_extender_1_out, 2'b00}), .in1(bit_extender_2_out), .in2(bit_extender_3_out),
    .in3(random_1_out), .out(Constant_k), .sel(k_selector), .en(k_En));

  // Other names for the same wires on the sheet: clk = Clock; cmp_zero[1:0] = Compare_to_Zero_Selector;
  //   cmp_zero_En = Compare_to_Zero_Enable; DI_Selector[2:0] = Data_Input_Selector; direction[25:0] = destination_jmp;
  //   Jump[25:0] = destination_jmp; beq = Compare_to_other_register_Selector;
  //   equal = Compare_to_other_register_Selector; equal_En = Compare_to_other_register_Enable;
  //   halt = halt__Stop_program; Hi_Lo_Write = Enable_Hi_Lo; IF = Inmediate_operation_enable;
  //   Inmediato[15:0] = Constant; jmp = jmp__Instruccion_de_Salto_con_Constante;
  //   jr = jr__Instruccion_de_Salto_con_Registro; k[31:0] = Constant_k; lw = lw__load_word; nor = F_nor;
  //   Operation[3:0] = Operation_ALU; SA[4:0] = Register_A_Selector; SB[4:0] = Register_B_Selector; sub = F_sub;
  //   SW[4:0] = Selector_of_the_register_to_write; sw_t = sw__store_word; tty = tty__Write_to_terminal;
  //   type[2:0] = Operation_Type

  // Notes on the sheet:
  //   Inputs
  //   Outputs
  //   ALU Operations
  //   Aritmetic Operators
  //   Logic Operators
  //   Mul & Div
  //   R-Type
  //   Operation Code
  //   Send  Outpus
  //   No Operation
  //   111 111 :
  //   Control and Register
  //   Move from Hi & Lo
  //   Stack Operations
  //   Special Instructions
  //   Jump Register
  //   Di_Selector RegisterFile
  //   Enable Hi&Lo
  //   I-Type
  //   Inmediate Operations
  //   Branch Operations
  //   Word Operators
  //   Send  Outpus
  //   Inmediate Flag
  //   Branch Flag
  //   Compare Flag
  //   J-Type
  //   Jump
  //   Control Arithmetic Operations
  //   Set Aritmetic Operations
  //   Operation-ALU Encoder
  //   Control Others Operations
  //   Set Operation Type
  //   Set Constant k
endmodule

// RF
module RegisterFile (
  input  [4:0] DA,
  input  RW,
  input  Rst,
  input  [31:0] DI,
  input  CLK,
  input  Right_Hi___Low,
  input  [4:0] SA,
  input  [4:0] SB,
  input  Ld_SP,
  input  [31:0] In_SP,
  input  [31:0] In_Hi,
  input  [31:0] In_Low,
  output [31:0] Stack_Pointer,
  output [31:0] A,
  output [31:0] Hi,
  output [31:0] B,
  output [31:0] Low
);

  wire L00, L01, L02, L03, L04, L05, L06, L07, L08, L09, L10, L11, L12, L13, L14, L15, L16, L17, L18, L19,
       L20, L21, L22, L23, L24, L25, L26, L27, L28, L29, L30, L31;
  wire [31:0] I_SP, R00, R01, R02, R03, R04, R05, R06, R07, R08, R09, R10, R11, R12, R13, R14, R15, R16, R17,
       R18, R19, R20, R21, R22, R23, R24, R25, R26, R27, R28, R29, R30, R31;

  Demultiplexer #(.select(5), .enable("false")) demultiplexer_1 (
    .out0(L00), .out1(L01), .out2(L02), .out3(L03), .out4(L04), .out5(L05), .out6(L06), .out7(L07),
    .out8(L08), .out9(L09), .out10(L10), .out11(L11), .out12(L12), .out13(L13), .out14(L14), .out15(L15),
    .out16(L16), .out17(L17), .out18(L18), .out19(L19), .out20(L20), .out21(L21), .out22(L22), .out23(L23),
    .out24(L24), .out25(L25), .out26(L26), .out27(L27), .out28(L28), .out29(L29), .out30(L30), .out31(L31),
    .in(RW), .sel(DA));
  Register #(.width(32)) u_R00 (.D({32{1'b0}}), .en(L00), .Q(R00), .clk(CLK), .clr(Rst));
  Register #(.width(32)) u_R08 (.D(DI), .en(L08), .Q(R08), .clk(CLK), .clr(Rst));
  Register #(.width(32)) u_R16 (.D(DI), .en(L16), .Q(R16), .clk(CLK), .clr(Rst));
  Register #(.width(32)) u_R24 (.D(DI), .en(L24), .Q(R24), .clk(CLK), .clr(Rst));
  Register #(.width(32)) u_R01 (.D(DI), .en(L01), .Q(R01), .clk(CLK), .clr(Rst));
  Register #(.width(32)) u_R09 (.D(DI), .en(L09), .Q(R09), .clk(CLK), .clr(Rst));
  Register #(.width(32)) u_R17 (.D(DI), .en(L17), .Q(R17), .clk(CLK), .clr(Rst));
  Register #(.width(32)) u_R25 (.D(DI), .en(L25), .Q(R25), .clk(CLK), .clr(Rst));
  Multiplexer #(.select(5), .width(32), .enable("false")) multiplexer_1 (
    .in0(R00), .in1(R01), .in2(R02), .in3(R03), .in4(R04), .in5(R05), .in6(R06), .in7(R07), .in8(R08),
    .in9(R09), .in10(R10), .in11(R11), .in12(R12), .in13(R13), .in14(R14), .in15(R15), .in16(R16),
    .in17(R17), .in18(R18), .in19(R19), .in20(R20), .in21(R21), .in22(R22), .in23(R23), .in24(R24),
    .in25(R25), .in26(R26), .in27(R27), .in28(R28), .in29(R29), .in30(R30), .in31(R31), .out(A), .sel(SA));
  Register #(.width(32)) u_R02 (.D(DI), .en(L02), .Q(R02), .clk(CLK), .clr(Rst));
  Register #(.width(32)) u_R10 (.D(DI), .en(L10), .Q(R10), .clk(CLK), .clr(Rst));
  Register #(.width(32)) u_R18 (.D(DI), .en(L18), .Q(R18), .clk(CLK), .clr(Rst));
  Register #(.width(32)) u_R26 (.D(DI), .en(L26), .Q(R26), .clk(CLK), .clr(Rst));
  Register #(.width(32)) u_R03 (.D(DI), .en(L03), .Q(R03), .clk(CLK), .clr(Rst));
  Register #(.width(32)) u_R11 (.D(DI), .en(L11), .Q(R11), .clk(CLK), .clr(Rst));
  Register #(.width(32)) u_R19 (.D(DI), .en(L19), .Q(R19), .clk(CLK), .clr(Rst));
  Register #(.width(32)) u_R27 (.D(DI), .en(L27), .Q(R27), .clk(CLK), .clr(Rst));
  Multiplexer #(.select(5), .width(32), .enable("false")) multiplexer_2 (
    .in0(R00), .in1(R01), .in2(R02), .in3(R03), .in4(R04), .in5(R05), .in6(R06), .in7(R07), .in8(R08),
    .in9(R09), .in10(R10), .in11(R11), .in12(R12), .in13(R13), .in14(R14), .in15(R15), .in16(R16),
    .in17(R17), .in18(R18), .in19(R19), .in20(R20), .in21(R21), .in22(R22), .in23(R23), .in24(R24),
    .in25(R25), .in26(R26), .in27(R27), .in28(R28), .in29(R29), .in30(R30), .in31(R31), .out(B), .sel(SB));
  Register #(.width(32)) u_R04 (.D(DI), .en(L04), .Q(R04), .clk(CLK), .clr(Rst));
  Register #(.width(32)) u_R12 (.D(DI), .en(L12), .Q(R12), .clk(CLK), .clr(Rst));
  Register #(.width(32)) u_R20 (.D(DI), .en(L20), .Q(R20), .clk(CLK), .clr(Rst));
  Register #(.width(32)) u_R28 (.D(DI), .en(L28), .Q(R28), .clk(CLK), .clr(Rst));
  Register #(.width(32)) u_R05 (.D(DI), .en(L05), .Q(R05), .clk(CLK), .clr(Rst));
  Register #(.width(32)) u_R13 (.D(DI), .en(L13), .Q(R13), .clk(CLK), .clr(Rst));
  Register #(.width(32)) u_R21 (.D(DI), .en(L21), .Q(R21), .clk(CLK), .clr(Rst));
  Register #(.width(32)) u_R29 (.D(DI), .en(L29), .Q(R29), .clk(CLK), .clr(Rst));
  Register #(.width(32)) u_R06 (.D(DI), .en(L06), .Q(R06), .clk(CLK), .clr(Rst));
  Register #(.width(32)) u_R14 (.D(DI), .en(L14), .Q(R14), .clk(CLK), .clr(Rst));
  Register #(.width(32)) u_R22 (.D(DI), .en(L22), .Q(R22), .clk(CLK), .clr(Rst));
  Register #(.width(32)) u_R30 (.D(DI), .en(L30), .Q(R30), .clk(CLK), .clr(Rst));
  Register #(.width(32)) u_R07 (.D(DI), .en(L07), .Q(R07), .clk(CLK), .clr(Rst));
  Register #(.width(32)) u_R15 (.D(DI), .en(L15), .Q(R15), .clk(CLK), .clr(Rst));
  Register #(.width(32)) u_R23 (.D(DI), .en(L23), .Q(R23), .clk(CLK), .clr(Rst));
  Register #(.width(32)) u_R31 (.D(I_SP), .en(Ld_SP), .Q(Stack_Pointer), .clk(CLK), .clr(Rst));
  Register #(.width(32)) R_Hi (.D(In_Hi), .en(Right_Hi___Low), .Q(Hi), .clk(CLK), .clr(Rst));
  Register #(.width(32)) R_low (.D(In_Low), .en(Right_Hi___Low), .Q(Low), .clk(CLK), .clr(Rst));

  // Other names for the same wires on the sheet: I_hi[31:0] = In_Hi; I_low[31:0] = In_Low; R_Hi[31:0] = Hi;
  //   R_low[31:0] = Low; RSP[31:0] = Stack_Pointer; W_hl = Right_Hi___Low

  // Notes on the sheet:
  //   INPUT
  //   Zero Register
  //   OUTPUT
  //   REGISTERS
  //   Stack Pointer
  //   Hight Low
  //   Right Low
endmodule

// 1
module Branch_Control (
  input  [25:0] Destiny,
  input  [31:0] Program_Counter,
  input  [1:0] PC_selector,
  input  SF,
  input  [31:0] RS,
  input  ZF,
  input  [15:0] Inmediate_Constant,
  input  [2:0] Branch_Selector,
  output [31:0] PC_prime
);

  wire Branch, not_1_out, not_2_out, or_1_out;
  wire [31:0] adder_1_out, Inmediate_Constant_t, multiplexer_2_out, shifter_1_out;

  assign Inmediate_Constant_t = {{16{1'b0}}, Inmediate_Constant};  // Bit_Extender bit_extender_1
  Adder #(.width(32)) adder_1 (.a(Program_Counter), .b(32'h4), .out(adder_1_out));  // open: cin, cout
  not not_1 (not_1_out, ZF);
  not not_2 (not_2_out, SF);
  Multiplexer #(.select(3), .enable("false")) multiplexer_1 (
    .in0(ZF), .in1(not_1_out), .in2(not_2_out), .in3(or_1_out), .in4(SF), .out(Branch), .sel(Branch_Selector));  // open: in5, in6, in7
  or or_1 (or_1_out, not_2_out, ZF);
  Multiplexer #(.width(32), .enable("false")) multiplexer_2 (
    .in0(adder_1_out), .out(multiplexer_2_out), .sel(Branch));  // open: in1
  Shifter #(.width(32)) shifter_1 (.in(Inmediate_Constant_t), .\dist (5'b00010), .out(shifter_1_out));
  Multiplexer #(.select(2), .width(32), .enable("false")) multiplexer_3 (
    .in0(adder_1_out), .in1(multiplexer_2_out), .in2({Program_Counter[31:28], Destiny, 2'b00}), .in3(RS),
    .out(PC_prime), .sel(PC_selector));

  // Other names for the same wires on the sheet: PC[31:0] = Program_Counter

  // Notes on the sheet:
  //   Inputs:
  //   Output:
endmodule

module Control_Unit (
  input  [5:0] in_1,
  input  [5:0] in_2,
  input  in_3,
  input  in_4,
  input  in_5,
  input  in_6,
  input  in_7,
  output UseRam,
  output WriteRam,
  output Halt,
  output TTY_ENABLE,
  output [3:0] operation_sel,
  output operand_A_sel,
  output [1:0] operand_B_sel,
  output DA_SEL,
  output DI_SEL,
  output WRF,
  output W_HI_LO,
  output W_SP,
  output [1:0] PC_SEL,
  output [1:0] Branch_SEL,
  output LD_PC,
  output LD_ID,
  output [1:0] Addres_SEL,
  output Data_SEL
);

  wire add, addi, \and , andi, beq, bgtz, blez, bltz, bne, demultiplexer_1_out0, demultiplexer_1_out1,
       demultiplexer_2_out0, demultiplexer_3_out0, demultiplexer_3_out1, div, divu, EXCECUTED, EXECUTING_q,
       halt_t, IDLE_q, J, jr, kbd, lw, mfhi, mflo, mult, mulu, nop, \nor , \or , or_1_out, or_2_out, ori,
       pop, push, READING_q, RESET_EXECUTORS, rnd, slt, slti, sltiu, sltu, sub, sw, tty, \xor , xori;
  wire [1:0] operand_B_SEL1, operand_B_SEL2;
  wire [3:0] op_sel_1, op_sel_2, op_sel_3;

  DECODER decoder_1 (
    .in_1(in_1), .in_2(in_2), .nop(nop), .add(add), .sub(sub), .mult(mult), .mulu(mulu), .div(div),
    .divu(divu), .slt(slt), .sltu(sltu), .\and (\and ), .\or (\or ), .\xor (\xor ), .\nor (\nor ), .pop(pop),
    .push(push), .mfhi(mfhi), .mflo(mflo), .jr(jr), .addi(addi), .sltiu(sltiu), .slti(slti), .ori(ori),
    .andi(andi), .xori(xori), .lw(lw), .sw(sw), .beq(beq), .bne(bne), .blez(blez), .bgtz(bgtz), .bltz(bltz),
    .J(J), .halt(halt_t), .tty(tty), .rnd(rnd), .kbd(kbd));
  D_Flip_Flop #(.trigger("falling")) IDLE (
    .clk(in_3), .D(demultiplexer_1_out0), .Q(IDLE_q), .preset(in_4));  // open: Qn, en, reset
  Demultiplexer #(.enable("false")) demultiplexer_1 (
    .out0(demultiplexer_1_out0), .out1(demultiplexer_1_out1), .in(IDLE_q), .sel(in_4));
  or or_1 (or_1_out, demultiplexer_2_out0, demultiplexer_1_out1, demultiplexer_3_out1);
  TYPE_AL type_al_1 (
    .in_1(add), .in_2(sub), .in_3(mult), .in_4(mulu), .in_5(div), .in_6(divu), .in_7(\and ), .in_8(\or ),
    .in_9(\nor ), .in_10(\xor ), .in_11(slt), .in_12(sltu), .Operation_Sel(op_sel_1));  // open: in_13, WRF, WH_L, LD_PC, end
  TYPE_INM type_inm_1 (
    .in_1(addi), .in_2(andi), .in_3(ori), .in_4(xori), .in_5(slti), .in_6(sltiu), .operand_sel(op_sel_2),
    .Operand_B(operand_B_SEL1));  // open: in_7, WRF, Pc_LD, End
  D_Flip_Flop #(.trigger("falling")) READING (.clk(in_3), .D(or_1_out), .Q(READING_q));  // open: Qn, preset, en, reset
  Demultiplexer #(.enable("false")) demultiplexer_2 (
    .out0(demultiplexer_2_out0), .out1(RESET_EXECUTORS), .in(READING_q), .sel(in_5));
  POP pop_1 (.in_4(in_3));  // open: in_2, in_3, out_5, out_6, out_7, out_8, out_9, out_10, out_11, out_12, in_1, out_13
  PUSH push_1 (
    .in_4(in_3), .out_10(operand_B_SEL2), .out_11(op_sel_3));  // open: in_2, in_3, out_5, out_6, out_7, out_8, out_9, out_13, out_14, in_1, Output
  or or_2 (or_2_out, demultiplexer_3_out0, RESET_EXECUTORS);
  LOAD_WORD load_word_1 (.in_4(in_3));  // open: in_2, in_3, Output, Output_2, Output_3, DA_SEL, WRF, LD_PC, in_1, out_11
  SAVE_WORD save_word_1 (.in_4(in_3));  // open: in_2, in_3, Output, Output_2, LD_PC, in_1, Output_3
  Demultiplexer #(.enable("false")) demultiplexer_3 (
    .out0(demultiplexer_3_out0), .out1(demultiplexer_3_out1), .in(EXECUTING_q), .sel(EXCECUTED));
  D_Flip_Flop #(.trigger("falling")) EXECUTING (
    .clk(in_3), .D(or_2_out), .Q(EXECUTING_q));  // open: Qn, preset, en, reset
  TYPE_HI_LO type_hi_lo_1 (.mfhi(mfhi), .mflo(mflo));  // open: enable, WRF, LD_PC, DI_SEL, End
  TYPE_SPECIAL type_special_1 (
    .halt(halt_t), .tty(tty), .\rand (rnd), .kbd(kbd));  // open: enable, LD_PC, halt_2, TTY_ENABLE, KBB_ENABLE, DI_SEL, WRF, END
  TYPE_BRANCH type_branch_1 (
    .in_2(beq), .in_3(bne), .in_4(blez), .in_5(bgtz), .in_6(bltz), .in_7(J), .in_8(jr), .in_1(nop));  // open: in_9, Branch_sel, Pc_Sel, Ld_PC, End
  assign operation_sel = op_sel_1 | op_sel_2 | op_sel_3;  // OR_Gate or_3, 4 bits wide

  // Other names for the same wires on the sheet: CLK = in_3; DATA_READ = in_6; FunCode[5:0] = in_2; INST_READ = in_5;
  //   OpCode[5:0] = in_1; Start = in_4; WRITTEN = in_7

  // Notes on the sheet:
  //   INPUTS
  //   DECODER
  //   IDLE
  //   FETCH
  //   EXECUTORS
  //   CONTROL UNIT FLOW 
  //   EXECUTE
endmodule

module TYPE_INM (
  input  in_1,
  input  in_2,
  input  in_3,
  input  in_4,
  input  in_5,
  input  in_6,
  input  in_7,
  output [3:0] operand_sel,
  output [1:0] Operand_B,
  output WRF,
  output Pc_LD,
  output End
);

  wire or_1_out;

  or or_1 (or_1_out, in_1, in_6);
  and and_1 (Operand_B[1], or_1_out, in_7);
  Priority_Encoder #(.select(4)) priority_encoder_1 (
    .in0(in_1), .in2(in_2), .in3(in_3), .in5(in_4), .in6(in_5), .in7(in_6), .out(operand_sel));  // open: in1, in4, in8, in9, in10, in11, in12, in13, in14, in15, gs, en_out, en_in

  assign End = in_7;
  assign Operand_B[0] = in_7;
  assign Pc_LD = in_7;
  assign WRF = in_7;

  // Other names for the same wires on the sheet: addi = in_1; andi = in_2; op_sel[3:0] = operand_sel; enable = in_7;
  //   ori = in_3; slti = in_5; sltiu = in_6; xori = in_4
endmodule

module TYPE_BRANCH (
  input  in_1,
  input  in_2,
  input  in_3,
  input  in_4,
  input  in_5,
  input  in_6,
  input  in_7,
  input  in_8,
  input  in_9,
  output [2:0] Branch_sel,
  output [1:0] Pc_Sel,
  output Ld_PC,
  output End
);

  wire not_1_out, not_2_out, not_3_out, not_4_out, not_5_out, not_6_out;
  wire [1:0] and_1_out;

  Priority_Encoder priority_encoder_1 (
    .in0(in_2), .in1(in_3), .in2(in_5), .in3(in_4), .in4(in_6), .out(Branch_sel));  // open: in5, in6, in7, en_in, gs, en_out
  not not_1 (not_1_out, in_2);
  not not_2 (not_2_out, in_3);
  not not_3 (not_3_out, in_4);
  not not_4 (not_4_out, in_5);
  not not_5 (not_5_out, in_6);
  not not_6 (not_6_out, in_7);
  and and_1 (and_1_out[0], not_1_out, not_2_out, not_3_out, not_4_out, not_5_out, in_9);
  and and_2 (and_1_out[1], not_6_out, in_9);
  Multiplexer #(.width(2), .enable("false")) multiplexer_1 (.in0(and_1_out), .in1(2'b00), .out(Pc_Sel), .sel(in_1));

  assign End = in_9;
  assign Ld_PC = in_9;

  // Other names for the same wires on the sheet: Beq = in_2; Bgtz = in_5; Blez = in_4; Bltz = in_6; Bne = in_3;
  //   enable = in_9; j = in_7; jr = in_8; nop = in_1
endmodule

module TYPE_AL (
  input  in_1,
  input  in_2,
  input  in_3,
  input  in_4,
  input  in_5,
  input  in_6,
  input  in_7,
  input  in_8,
  input  in_9,
  input  in_10,
  input  in_11,
  input  in_12,
  input  in_13,
  output [3:0] Operation_Sel,
  output WRF,
  output WH_L,
  output LD_PC,
  output \end 
);

  wire not_1_out, or_1_out;

  Priority_Encoder #(.select(4)) priority_encoder_1 (
    .in0(in_1), .in1(in_2), .in2(in_7), .in3(in_8), .in4(in_9), .in5(in_10), .in6(in_11), .in7(in_12),
    .in8(in_4), .in9(in_3), .in10(in_6), .in11(in_5), .out(Operation_Sel));  // open: in12, in13, in14, in15, gs, en_out, en_in
  or or_1 (or_1_out, in_3, in_4, in_5, in_6);
  not not_1 (not_1_out, or_1_out);
  and and_1 (WRF, not_1_out, in_13);
  and and_2 (WH_L, in_13, or_1_out);

  assign \end  = in_13;
  assign LD_PC = in_13;

  // Other names for the same wires on the sheet: add = in_1; and = in_7; div = in_5; divu = in_6; enable = in_13;
  //   mul = in_3; mulu = in_4; nor = in_9; or = in_8; slt = in_11; sltu = in_12; sub = in_2; xor = in_10
endmodule

module TYPE_HI_LO (
  input  mfhi,
  input  mflo,
  input  enable,
  output WRF,
  output LD_PC,
  output [2:0] DI_SEL,
  output End
);

  Multiplexer #(.width(3)) multiplexer_1 (.in0(3'b001), .in1(3'b010), .out(DI_SEL), .sel(mfhi), .en(enable));

  assign End = enable;
  assign LD_PC = enable;
  assign WRF = enable;
endmodule

module DECODER (
  input  [5:0] in_1,
  input  [5:0] in_2,
  output nop,
  output add,
  output sub,
  output mult,
  output mulu,
  output div,
  output divu,
  output slt,
  output sltu,
  output \and ,
  output \or ,
  output \xor ,
  output \nor ,
  output pop,
  output push,
  output mfhi,
  output mflo,
  output jr,
  output addi,
  output sltiu,
  output slti,
  output ori,
  output andi,
  output xori,
  output lw,
  output sw,
  output beq,
  output bne,
  output blez,
  output bgtz,
  output bltz,
  output J,
  output halt,
  output tty,
  output rnd,
  output kbd
);

  wire _00, _01, _10, _11, and_1_out, and_11_out, and_12_out, and_29_out, and_32_out, and_33_out, and_34_out,
       and_47_out, comparator_2_eq, Especial, I, or_1_out, R, R_00, R_01, R_10;

  Comparator #(.width(6)) comparator_1 (.a(in_1), .b(6'b000010), .eq(J));  // open: gt, lt
  Comparator #(.width(6)) comparator_2 (.a(in_1), .b({6{1'b0}}), .eq(comparator_2_eq));  // open: gt, lt
  or or_1 (or_1_out, comparator_2_eq, and_1_out);
  and and_1 (and_1_out, in_1[5], in_1[4], in_1[3]);
  and and_2 (Especial, and_1_out, in_1[2]);
  and and_3 (I, ~or_1_out, ~J);  // AND_Gate
  and and_4 (R, or_1_out, ~Especial);  // AND_Gate
  and and_5 (_10, ~in_1[0], I, in_1[1]);  // AND_Gate
  and and_6 (_11, in_1[0], I, in_1[1]);
  and and_7 (_01, in_1[0], I, ~in_1[1]);  // AND_Gate
  and and_8 (_00, ~in_1[0], I, ~in_1[1]);  // AND_Gate
  and and_9 (mflo, ~in_2[3], R_01, in_2[1]);  // AND_Gate
  and and_10 (mfhi, ~in_2[3], R_01, ~in_2[1]);  // AND_Gate
  and and_11 (and_11_out, in_2[3], R_01, ~in_2[1]);  // AND_Gate
  and and_12 (and_12_out, in_2[3], R_01, in_2[1]);
  and and_13 (R_00, ~in_2[4], R, ~in_2[5]);  // AND_Gate
  and and_14 (R_10, ~in_2[4], R, in_2[5]);  // AND_Gate
  and and_15 (R_01, in_2[4], R, ~in_2[5]);  // AND_Gate
  and and_16 (divu, and_12_out, in_2[0]);
  and and_17 (div, and_12_out, ~in_2[0]);  // AND_Gate
  and and_18 (mulu, and_11_out, in_2[0]);
  and and_19 (mult, and_11_out, ~in_2[0]);  // AND_Gate
  and and_20 (addi, ~in_1[2], _00, in_1[3]);  // AND_Gate
  and and_21 (andi, in_1[2], _00, in_1[3]);
  and and_22 (beq, in_1[2], _00, ~in_1[3]);  // AND_Gate
  and and_23 (sltiu, ~in_1[5], _11, in_1[3]);  // AND_Gate
  and and_24 (sw, in_1[5], _11, in_1[3]);
  and and_25 (lw, in_1[5], _11, ~in_1[3]);  // AND_Gate
  and and_26 (bgtz, ~in_1[5], _11, ~in_1[3]);  // AND_Gate
  and and_27 (jr, ~in_2[0], R_00, in_2[3]);  // AND_Gate
  and and_28 (push, in_2[0], R_00, ~in_2[3]);  // AND_Gate
  and and_29 (and_29_out, ~in_2[0], R_00, ~in_2[3]);  // AND_Gate
  and and_30 (pop, and_29_out, in_1[5]);
  and and_31 (nop, and_29_out, ~in_1[5]);  // AND_Gate
  and and_32 (and_32_out, ~in_2[3], R_10, ~in_2[2]);  // AND_Gate
  and and_33 (and_33_out, in_2[3], R_10, in_2[1]);
  and and_34 (and_34_out, ~in_2[3], R_10, in_2[2]);  // AND_Gate
  and and_35 (\xor , in_2[3], R_10, ~in_2[1]);  // AND_Gate
  and and_36 (slti, ~in_1[2], _10, in_1[3]);  // AND_Gate
  and and_37 (xori, in_1[2], _10, in_1[3]);
  and and_38 (blez, in_1[2], _10, ~in_1[3]);  // AND_Gate
  and and_39 (bne, in_1[2], _01, ~in_1[3]);  // AND_Gate
  and and_40 (ori, in_1[2], _01, in_1[3]);
  and and_41 (bltz, ~in_1[2], _01, ~in_1[3]);  // AND_Gate
  and and_42 (sub, in_2[1], and_32_out);
  and and_43 (add, ~in_2[1], and_32_out);  // AND_Gate
  and and_44 (sltu, and_33_out, in_2[0]);
  and and_45 (slt, ~in_2[0], and_33_out);  // AND_Gate
  and and_46 (\and , and_34_out, ~in_2[0]);  // AND_Gate
  and and_47 (and_47_out, and_34_out, in_2[0]);
  and and_48 (\nor , and_47_out, in_2[1]);
  and and_49 (\or , ~in_2[1], and_47_out);  // AND_Gate
  and and_50 (halt, in_2[0], Especial, in_2[1]);
  and and_51 (tty, in_2[0], Especial, ~in_2[1]);  // AND_Gate
  and and_52 (rnd, ~in_2[0], Especial, in_2[1]);  // AND_Gate
  and and_53 (kbd, ~in_2[0], Especial, ~in_2[1]);  // AND_Gate

  // Other names for the same wires on the sheet: F_bit1 = in_2[0]; FuncCode[5:0] = in_2; F_bit2 = in_2[1];
  //   F_bit3 = in_2[2]; F_bit4 = in_2[3]; OpCode[5:0] = in_1; Bit3 = in_1[2]; Bit4 = in_1[3]; Bit6 = in_1[5]

  // Notes on the sheet:
  //   Tipo R
endmodule

module RamManager (
  input  [31:0] Addres_In,
  input  [31:0] Ram_out_0,
  input  [31:0] Ram_out_1,
  input  [31:0] Ram_out_2,
  input  [31:0] Ram_out_3,
  input  [3:0] Read_Time,
  input  Clk,
  input  Rst,
  input  [3:0] Write_Time,
  input  Start,
  input  R_W,
  output [31:0] From_RAM,
  output [3:0] Mask,
  output [15:0] ADDR,
  output RAMReady,
  output Chip_Select,
  output RAM_Write
);

  wire Clk_t, comparator_1_lt, demultiplexer_1_out0, demultiplexer_1_out1, IsFetch, or_2_out, Wait_q;
  wire [3:0] counter_1_q, Time;
  wire [31:0] RAM_OUT_0_t, RAM_OUT_1_t, RAM_OUT_2_t, RAM_OUT_3_t;

  Multiplexer #(.width(4), .enable("false")) multiplexer_1 (.in0(Read_Time), .in1(Write_Time), .out(Time), .sel(R_W));
  LittleEndianSwap littleendianswap_1 (.Input(Ram_out_0), .Output(RAM_OUT_0_t));
  LittleEndianSwap littleendianswap_2 (.Input(Ram_out_1), .Output(RAM_OUT_1_t));
  LittleEndianSwap littleendianswap_3 (.Input(Ram_out_2), .Output(RAM_OUT_2_t));
  LittleEndianSwap littleendianswap_4 (.Input(Ram_out_3), .Output(RAM_OUT_3_t));
  D_Flip_Flop Wait (.clk(Clk), .D(demultiplexer_1_out0), .Q(Wait_q));  // open: Qn, preset, en, reset
  or or_1 (Chip_Select, Wait_q, Start);
  Counter #(.width(4), .max('hf)) counter_1 (
    .count(Chip_Select), .Q(counter_1_q), .clk(Clk), .clr(or_2_out));  // open: load, D, carry
  or or_2 (or_2_out, Rst, RAMReady);
  Demultiplexer #(.enable("false")) demultiplexer_1 (
    .out0(demultiplexer_1_out0), .out1(demultiplexer_1_out1), .in(Chip_Select), .sel(IsFetch));
  Comparator #(.width(4), .mode("unsigned")) comparator_1 (
    .a(counter_1_q), .b(Time), .lt(comparator_1_lt));  // open: gt, eq
  not not_1 (IsFetch, comparator_1_lt);
  D_Flip_Flop End (.clk(Clk_t), .D(demultiplexer_1_out1), .Q(RAMReady));  // open: Qn, preset, en, reset
  Decoder #(.select(2), .enable("false")) decoder_1 (
    .out0(Mask[0]), .out1(Mask[1]), .out2(Mask[2]), .out3(Mask[3]), .sel(Addres_In[1:0]));
  Multiplexer #(.select(2), .width(32), .enable("false")) multiplexer_2 (
    .in0(RAM_OUT_0_t), .in1(RAM_OUT_1_t), .in2(RAM_OUT_2_t), .in3(RAM_OUT_3_t), .out(From_RAM),
    .sel(Addres_In[1:0]));
  and and_1 (RAM_Write, R_W, Chip_Select);

  assign ADDR = Addres_In[17:2];

  // Other names for the same wires on the sheet: Bank[1:0] = Addres_In[1:0]; Block[15:0] = Addres_In[17:2];
  //   Clear = RAMReady; End = RAMReady; Count = Chip_Select; CS = Chip_Select; RAM_Wr = Chip_Select; RW = R_W

  // Notes on the sheet:
  //   ADDRESS
  //   DATA FROM RAM
  //   RAM TIMING
  //   CONTROL SIGNALS
  //   TIMER
  //   FLOW CONTROL
endmodule

module LittleEndianSwap (
  input  [31:0] Input,
  output [31:0] Output
);


  assign Output = {Input[3:0], Input[7:4], Input[11:8], Input[15:12], Input[19:16], Input[23:20], Input[27:24], Input[31:28]};
endmodule

module LOAD_WORD (
  input  in_1,
  input  in_2,
  input  in_3,
  input  in_4,
  output [1:0] Output,
  output Output_2,
  output Output_3,
  output [2:0] DA_SEL,
  output WRF,
  output LD_PC,
  output out_11
);

  wire demultiplexer_1_out0, demultiplexer_3_out0, demultiplexer_3_out1, IDLE_q, or_1_out, or_2_out,
       or_3_out, WAIT_q;

  D_Flip_Flop #(.trigger("falling")) IDLE (
    .clk(in_4), .D(demultiplexer_1_out0), .Q(IDLE_q), .preset(in_2));  // open: Qn, en, reset
  or or_1 (or_1_out, IDLE_q, demultiplexer_3_out1);
  Demultiplexer #(.enable("false")) demultiplexer_1 (
    .out0(demultiplexer_1_out0), .out1(Output[1]), .in(or_1_out), .sel(in_2));
  or or_2 (or_2_out, Output_2, Output[1]);
  D_Flip_Flop #(.trigger("falling")) WAIT (.clk(in_4), .D(or_2_out), .Q(WAIT_q));  // open: Qn, preset, en, reset
  Demultiplexer #(.enable("false")) demultiplexer_2 (.out0(Output_2), .out1(LD_PC), .in(WAIT_q), .sel(in_1));
  or or_3 (or_3_out, demultiplexer_3_out0, LD_PC);
  Multiplexer #(.width(3), .enable("false")) multiplexer_1 (.in0(3'b000), .in1(3'b011), .out(DA_SEL), .sel(LD_PC));
  D_Flip_Flop #(.trigger("falling")) END (.clk(in_4), .D(or_3_out), .Q(out_11));  // open: Qn, preset, en, reset
  Demultiplexer #(.enable("false")) demultiplexer_3 (
    .out0(demultiplexer_3_out0), .out1(demultiplexer_3_out1), .in(out_11), .sel(in_3));

  assign Output[0] = Output[1];
  assign Output_3 = LD_PC;
  assign WRF = LD_PC;

  // Other names for the same wires on the sheet: CLK = in_4; DA_SEL_t = LD_PC; EN_DI_SEL = LD_PC; en_RAM = Output_2;
  //   enable = in_2; END = out_11; operand_B_Selector[1:0] = {2{Output[1]}}; RamReady = in_1; RST = in_3
endmodule

module SAVE_WORD (
  input  in_1,
  input  in_2,
  input  in_3,
  input  in_4,
  output [1:0] Output,
  output Output_2,
  output LD_PC,
  output Output_3
);

  wire demultiplexer_1_out0, demultiplexer_3_out0, demultiplexer_3_out1, IDLE_q, or_1_out, or_2_out,
       or_3_out, WAIT_q;

  D_Flip_Flop #(.trigger("falling")) IDLE (
    .clk(in_4), .D(demultiplexer_1_out0), .Q(IDLE_q), .preset(in_2));  // open: Qn, en, reset
  Demultiplexer #(.enable("false")) demultiplexer_1 (
    .out0(demultiplexer_1_out0), .out1(Output[1]), .in(or_1_out), .sel(in_2));
  or or_1 (or_1_out, IDLE_q, demultiplexer_3_out1);
  or or_2 (or_2_out, Output_2, Output[1]);
  D_Flip_Flop #(.trigger("falling")) WAIT (.clk(in_4), .D(or_2_out), .Q(WAIT_q));  // open: Qn, preset, en, reset
  Demultiplexer #(.enable("false")) demultiplexer_2 (.out0(Output_2), .out1(LD_PC), .in(WAIT_q), .sel(in_1));
  or or_3 (or_3_out, demultiplexer_3_out0, LD_PC);
  D_Flip_Flop #(.trigger("falling")) END (.clk(in_4), .D(or_3_out), .Q(Output_3));  // open: Qn, preset, en, reset
  Demultiplexer #(.enable("false")) demultiplexer_3 (
    .out0(demultiplexer_3_out0), .out1(demultiplexer_3_out1), .in(Output_3), .sel(in_3));

  assign Output[0] = Output[1];

  // Other names for the same wires on the sheet: CLK = in_4; en_RAM = Output_2; W_RAM = Output_2; enable = in_2;
  //   END = Output_3; operand_B_Selector[1:0] = {2{Output[1]}}; RAM_Data_SEL = Output[1]; RamReady = in_1; RST = in_3
endmodule

module POP (
  input  in_1,
  input  in_2,
  input  in_3,
  input  in_4,
  output out_5,
  output [1:0] out_6,
  output [2:0] out_7,
  output out_8,
  output [1:0] out_9,
  output out_10,
  output out_11,
  output out_12,
  output out_13
);

  wire demultiplexer_1_out0, demultiplexer_1_out1, demultiplexer_3_out0, demultiplexer_3_out1, IDLE_q,
       or_1_out, or_2_out, or_3_out, undriven, WAIT_q;

  D_Flip_Flop #(.trigger("falling")) IDLE (
    .clk(in_4), .D(demultiplexer_1_out0), .Q(IDLE_q), .preset(in_2));  // open: Qn, en, reset
  or or_1 (or_1_out, IDLE_q, demultiplexer_3_out1);
  Demultiplexer #(.enable("false")) demultiplexer_1 (
    .out0(demultiplexer_1_out0), .out1(demultiplexer_1_out1), .in(or_1_out), .sel(in_2));
  or or_2 (or_2_out, out_5, demultiplexer_1_out1);
  D_Flip_Flop #(.trigger("falling")) WAIT (.clk(in_4), .D(or_2_out), .Q(WAIT_q));  // open: Qn, preset, en, reset
  Demultiplexer #(.enable("false")) demultiplexer_2 (.out0(out_5), .out1(out_8), .in(WAIT_q), .sel(in_1));
  Multiplexer #(.width(3), .enable("false")) multiplexer_1 (.in0(3'b000), .in1(3'b011), .out(out_7), .sel(out_8));
  Multiplexer #(.width(2), .enable("false")) multiplexer_2 (.in0(2'b00), .in1(2'b01), .out(out_9), .sel(out_8));
  or or_3 (or_3_out, demultiplexer_3_out0, out_8);
  Demultiplexer #(.enable("false")) demultiplexer_3 (
    .out0(demultiplexer_3_out0), .out1(demultiplexer_3_out1), .in(out_13), .sel(in_3));
  D_Flip_Flop #(.trigger("falling")) END (
    .clk(in_4), .D(or_3_out), .Q(out_13), .reset(undriven));  // open: Qn, preset, en

  assign out_6 = {2{out_5}};
  assign out_10 = out_8;
  assign out_11 = out_8;
  assign out_12 = out_8;

  // Other names for the same wires on the sheet: ADDR_SEL[1:0] = {2{out_5}}; en_RAM = out_5; CLK = in_4;
  //   enable = in_2; END = out_13; EN_DI_SEL = out_8; EN_operand_B_Selector = out_8; LD_PC = out_8;
  //   operand_A_Selector = out_8; W_RF = out_8; W_SP = out_8; RamReady = in_1; RST = in_3
endmodule

module PUSH (
  input  in_1,
  input  in_2,
  input  in_3,
  input  in_4,
  output out_5,
  output out_6,
  output [1:0] out_7,
  output [2:0] out_8,
  output out_9,
  output [1:0] out_10,
  output [3:0] out_11,
  output Output,
  output out_13,
  output out_14
);

  wire demultiplexer_1_out0, demultiplexer_3_out0, demultiplexer_3_out1, IDLE_q, or_1_out, or_2_out,
       or_3_out, undriven, WAIT_q;

  D_Flip_Flop #(.trigger("falling")) IDLE (
    .clk(in_4), .D(demultiplexer_1_out0), .Q(IDLE_q), .preset(in_2));  // open: Qn, en, reset
  or or_1 (or_1_out, IDLE_q, demultiplexer_3_out1);
  Demultiplexer #(.enable("false")) demultiplexer_1 (
    .out0(demultiplexer_1_out0), .out1(out_9), .in(or_1_out), .sel(in_2));
  or or_2 (or_2_out, out_5, out_9);
  D_Flip_Flop #(.trigger("falling")) WAIT (.clk(in_4), .D(or_2_out), .Q(WAIT_q));  // open: Qn, preset, en, reset
  Demultiplexer #(.enable("false")) demultiplexer_2 (.out0(out_5), .out1(out_14), .in(WAIT_q), .sel(in_1));
  Multiplexer #(.width(4), .enable("false")) multiplexer_1 (.in0(4'b0000), .in1(4'b0001), .out(out_11), .sel(out_9));
  Multiplexer #(.width(2), .enable("false")) multiplexer_2 (.in0(2'b00), .in1(2'b01), .out(out_10), .sel(out_9));
  or or_3 (or_3_out, demultiplexer_3_out0, out_14);
  D_Flip_Flop #(.trigger("falling")) END (
    .clk(in_4), .D(or_3_out), .Q(Output), .reset(undriven));  // open: Qn, preset, en
  Demultiplexer #(.enable("false")) demultiplexer_3 (
    .out0(demultiplexer_3_out0), .out1(demultiplexer_3_out1), .in(Output), .sel(in_3));

  assign out_6 = out_5;
  assign out_7 = {2{out_5}};
  assign out_13 = out_9;

  // Other names for the same wires on the sheet: ADDR_SEL[1:0] = {2{out_5}}; en_RAM = out_5; W_RAM = out_5;
  //   CLK = in_4; DI_SEL[2:0] = out_8; enable = in_2; END = Output; LD_PC = out_14; en_operand_B_Selector = out_9;
  //   en_operation_sel = out_9; operand_A_Selector = out_9; W_SP = out_9; RamReady = in_1; RST = in_3
endmodule

module TYPE_SPECIAL (
  input  halt,
  input  tty,
  input  \rand ,
  input  kbd,
  input  enable,
  output LD_PC,
  output halt_2,
  output TTY_ENABLE,
  output KBB_ENABLE,
  output [2:0] DI_SEL,
  output WRF,
  output END
);

  wire or_1_out, or_2_out;

  or or_1 (or_1_out, \rand , kbd);
  and and_1 (DI_SEL[2], or_1_out, enable);
  and and_2 (halt_2, halt, enable);
  and and_3 (TTY_ENABLE, tty, enable);
  and and_4 (DI_SEL[0], kbd, enable);
  and and_5 (KBB_ENABLE, enable, kbd);
  or or_2 (or_2_out, \rand , kbd);
  and and_6 (WRF, or_2_out, enable);

  assign DI_SEL[1] = 1'b0;
  assign END = enable;
  assign LD_PC = enable;

  // Other names for the same wires on the sheet: rnd = \rand 
endmodule
